# Fritzing sketch PG5500 - Arduino Game Console - TFT ST7735 - Thumbstick (saved by Fritzing 0.9.3b)
breadboards: 1

parts:
  TFT1 = 2.2" TFT with MicroSD Breakout
  Part1 = Arduino Uno (Rev3)
  R3 = Resistor [tolerance=±5% resistance=220 package=THT]
  This_is_meant_to_be_the_DC_pin_on_the_TFT = Basic FET P-Channel [package="TO220 [THT]"]
  Part2 = Thumb Joystick

nets:
  N1: TFT1.MISO, Part1.D12/MISO
  N2: TFT1.SCK, Part1.D13/SCK
  N3: TFT1.MOSI, Part1.D11_PWM/MOSI
  N4: TFT1.CS, Part1.D10_PWM/SS
  N5: TFT1.SDCS, Part1.D4
  N6: TFT1.RST, Part1.D8
  VIN: TFT1.VIN, Part1.5V, R3.Pin_1, Part2.VCC
  GND: TFT1.GND, Part1.GND, Part2.GND
  N7: Part1.A0, Part2.HORZ
  N8: Part1.A1, Part2.VERT
  N9: Part1.D9_PWM, This_is_meant_to_be_the_DC_pin_on_the_TFT.gate
  N10: Part1.D2, R3.Pin_0, Part2.SEL

custom parts:
  2.2" TFT with MicroSD Breakout: 2.2" TFT Display with HX8340B Controller and MicroSD Card
